# Fritzing sketch NeoClock (saved by Fritzing 0.9.5d)
circuit board: 15cm x 10cm
breadboards: 1

parts:
  A1 = ESP32 DevKitc V4
  U2 = WS2812 RGB LED strip
  R1 = Resistor [tolerance=±5% resistance=470 package=THT]
  Bauteil2 = Real Time Clock Module - DS1307 RTC Breakout Board
  microSD1 = MicroSD Card Module
  Part1 = RFID-RC522-v3
  Part2 = Adafruit MAX98357A I2S 3W Class D Amplifier [part_number="Adafruit #3006"]
  Part3 = Adafruit Micro USB Breakout [part_number="Adafruit #1833"]
  C1 = Electrolytic Capacitor [capacitance=1000μF voltage=16V package="1010 [SMD, electrolytic]"]

nets (from the breadboard view):
  5V: A1.Pin_1, Bauteil2.5V, Part1.3.3V
  N1: A1.Pin_9, Part2.DIN
  N2: A1.Pin_10, Part2.LRCLK
  N3: A1.Pin_11, Part2.BCLK
  GND: A1.Pin_14, A1.Pin_32, A1.Pin_38, U2.GND, Bauteil2.GND, microSD1.GND, Part1.GND, Part2.GND, Part2.GAIN, Part3.GND, C1.-
  VCC: A1.Pin_19, U2.VCC, microSD1.VCC, Part2.VIN, Part3.VBUS, C1.+
  N4: A1.Pin_31, Part1.MISO
  N5: U2.DIN, R1.Pin_0
  N6: Bauteil2.SCL, Part1.RST
  N7: Bauteil2.SDA, Part1.IRQ

custom parts:
  ESP32 DevKitc V4: ESP32-DevKitC board with ESP32-WROOM-32 module. ESP32-DevKitC V4 is a small-sized ESP32-based development board produced by Espressif. Most of the pins on the ESP module are broken out to the pin headers on the board. The pins D0, D1, D2, D3, CMD and CLK are used internally for communication between ESP32 and SPI flash memory. They are grouped on both sides near the USB connector. Avoid using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
  WS2812 RGB LED strip: WS2812 strip
  RFID-RC522-v3: A simple China made RFID-RC522 Reader (6x4 cm); do check the pin labels, as this is a MFRC522 based clone.
  Adafruit MAX98357A I2S 3W Class D Amplifier: Listen to this good news - we now have an all in one digital audio amp breakout board that works incredibly well with the Raspberry Pi! If you're looking for an easy and low cost way to get you digital sound files bumpin' then the MAX08357 I2S Amp Breakout is for you. It takes standard I2S digital audio input and, not only decodes it into analog, but also amplifies it directly into a speaker.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
  Adafruit Micro USB Breakout: Simple but effective - this breakout board has a USB Micro-B connector, with all 5 pins broken out. Great for pairing with a microcontroller with USB support, or adding USB 5V power to a project. We use a micro-AB connector with through-hole shielding pads for an excellent strong connection - it won't rip off by accident! Comes with one fully assembled and tested micro B breakout PCB and a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
